// Digital circuit 8bit_BSD_TC_Adder.dig as structural Verilog
module _8bit_BSD_TC_Adder (
  input  [7:0] inTC,
  input  [15:0] inBSD,
  output [15:0] bsdOut,
  output [1:0] c
);

  Add add_1 (.a(inBSD[14]), .b(inBSD[15]), .c_i(inTC[7]), .s(bsdOut[15]), .c_o(c[0]));
  Add add_2 (.a(inBSD[12]), .b(inBSD[13]), .c_i(inTC[6]), .s(bsdOut[13]), .c_o(bsdOut[14]));
  Add add_3 (.a(inBSD[10]), .b(inBSD[11]), .c_i(inTC[5]), .s(bsdOut[11]), .c_o(bsdOut[12]));
  Add add_4 (.a(inBSD[8]), .b(inBSD[9]), .c_i(inTC[4]), .s(bsdOut[9]), .c_o(bsdOut[10]));
  Add add_5 (.a(inBSD[6]), .b(inBSD[7]), .c_i(inTC[3]), .s(bsdOut[7]), .c_o(bsdOut[8]));
  Add add_6 (.a(inBSD[4]), .b(inBSD[5]), .c_i(inTC[2]), .s(bsdOut[5]), .c_o(bsdOut[6]));
  Add add_7 (.a(inBSD[2]), .b(inBSD[3]), .c_i(inTC[1]), .s(bsdOut[3]), .c_o(bsdOut[4]));
  Add add_8 (.a(inBSD[0]), .b(inBSD[1]), .c_i(inTC[0]), .s(bsdOut[1]), .c_o(bsdOut[2]));

  assign bsdOut[0] = 1'b0;
  assign c[1] = 1'b1;
endmodule
