// Digital circuit conv5to8.dig as structural Verilog
module conv5to8 (
  input  [4:0] in,
  output [15:0] _10bdd
);


  assign _10bdd = {7'b1010101, in[4], 1'b1, in[3], 1'b1, in[2], 1'b1, in[1], 1'b1, in[0]};
endmodule
