// Digital circuit RomInterpretation.dig as structural Verilog
module RomInterpretation (
  input  [7:0] w3,
  input  [7:0] w4,
  input  [7:0] w5,
  input  [7:0] w6,
  input  [7:0] w7,
  input  [7:0] w8,
  input  [7:0] w9,
  input  [7:0] w1,
  input  [7:0] w2,
  input  clk,
  input  en,
  input  rst,
  output [4:0] o1,
  output [4:0] o2,
  output [4:0] o3,
  output [4:0] o4,
  output [4:0] o5,
  output [4:0] o6,
  output [4:0] o7,
  output [4:0] o8
);

  wire and_1_out, and_2_out, and_3_out, and_4_out, and_5_out, and_6_out, and_7_out, and_8_out,
       demultiplexer_2_out_0, demultiplexer_2_out_1, demultiplexer_2_out_2, demultiplexer_2_out_3,
       demultiplexer_2_out_4, demultiplexer_2_out_5, demultiplexer_2_out_6, demultiplexer_2_out_7,
       multiplexer_18_out, or_1_out, or_2_out, or_3_out, or_4_out, or_5_out, or_6_out, or_7_out, or_8_out,
       or_9_out, register_1_q, tc;
  wire [2:0] counter_1_out;
  wire [4:0] demultiplexer_1_out_0, demultiplexer_1_out_1, demultiplexer_1_out_2, demultiplexer_1_out_3,
       demultiplexer_1_out_4, demultiplexer_1_out_5, demultiplexer_1_out_6, demultiplexer_1_out_7,
       FilterKernel_d, multiplexer_10_out, multiplexer_11_out, multiplexer_12_out, multiplexer_13_out,
       multiplexer_14_out, multiplexer_15_out, multiplexer_16_out, multiplexer_17_out;
  wire [8:0] multiplexer_9_out;

  Counter #(.Bits(3)) counter_1 (.en(en), .C(clk), .clr(rst), .out(counter_1_out));  // open: ovf
  Multiplexer #(.Selector_Bits(3)) multiplexer_1 (
    .sel(counter_1_out), .in_0(w1[0]), .in_1(w1[1]), .in_2(w1[2]), .in_3(w1[3]), .in_4(w1[4]), .in_5(w1[5]),
    .in_6(w1[6]), .in_7(w1[7]), .out(multiplexer_9_out[8]));
  Multiplexer #(.Selector_Bits(3)) multiplexer_2 (
    .sel(counter_1_out), .in_0(w2[0]), .in_1(w2[1]), .in_2(w2[2]), .in_3(w2[3]), .in_4(w2[4]), .in_5(w2[5]),
    .in_6(w2[6]), .in_7(w2[7]), .out(multiplexer_9_out[7]));
  Multiplexer #(.Selector_Bits(3)) multiplexer_3 (
    .sel(counter_1_out), .in_0(w3[0]), .in_1(w3[1]), .in_2(w3[2]), .in_3(w3[3]), .in_4(w3[4]), .in_5(w3[5]),
    .in_6(w3[6]), .in_7(w3[7]), .out(multiplexer_9_out[6]));
  Multiplexer #(.Selector_Bits(3)) multiplexer_4 (
    .sel(counter_1_out), .in_0(w4[0]), .in_1(w4[1]), .in_2(w4[2]), .in_3(w4[3]), .in_4(w4[4]), .in_5(w4[5]),
    .in_6(w4[6]), .in_7(w4[7]), .out(multiplexer_9_out[5]));
  Multiplexer #(.Selector_Bits(3)) multiplexer_5 (
    .sel(counter_1_out), .in_0(w5[0]), .in_1(w5[1]), .in_2(w5[2]), .in_3(w5[3]), .in_4(w5[4]), .in_5(w5[5]),
    .in_6(w5[6]), .in_7(w5[7]), .out(multiplexer_9_out[4]));
  Multiplexer #(.Selector_Bits(3)) multiplexer_6 (
    .sel(counter_1_out), .in_0(w6[0]), .in_1(w6[1]), .in_2(w6[2]), .in_3(w6[3]), .in_4(w6[4]), .in_5(w6[5]),
    .in_6(w6[6]), .in_7(w6[7]), .out(multiplexer_9_out[3]));
  Multiplexer #(.Selector_Bits(3)) multiplexer_7 (
    .sel(counter_1_out), .in_0(w7[0]), .in_1(w7[1]), .in_2(w7[2]), .in_3(w7[3]), .in_4(w7[4]), .in_5(w7[5]),
    .in_6(w7[6]), .in_7(w7[7]), .out(multiplexer_9_out[2]));
  Multiplexer #(.Selector_Bits(3)) multiplexer_8 (
    .sel(counter_1_out), .in_0(w8[0]), .in_1(w8[1]), .in_2(w8[2]), .in_3(w8[3]), .in_4(w8[4]), .in_5(w8[5]),
    .in_6(w8[6]), .in_7(w8[7]), .out(multiplexer_9_out[1]));
  Multiplexer #(.Selector_Bits(3)) multiplexer_9 (
    .sel(counter_1_out), .in_0(w9[0]), .in_1(w9[1]), .in_2(w9[2]), .in_3(w9[3]), .in_4(w9[4]), .in_5(w9[5]),
    .in_6(w9[6]), .in_7(w9[7]), .out(multiplexer_9_out[0]));
  ROM #(.AddrBits(9), .Bits(5)) FilterKernel (.A(multiplexer_9_out), .sel(1'b1), .D(FilterKernel_d));
  Demultiplexer #(.Selector_Bits(3), .Bits(5)) demultiplexer_1 (
    .sel(counter_1_out), .in(FilterKernel_d), .out_0(demultiplexer_1_out_0), .out_1(demultiplexer_1_out_1),
    .out_2(demultiplexer_1_out_2), .out_3(demultiplexer_1_out_3), .out_4(demultiplexer_1_out_4),
    .out_5(demultiplexer_1_out_5), .out_6(demultiplexer_1_out_6), .out_7(demultiplexer_1_out_7));
  Multiplexer #(.Bits(5)) multiplexer_10 (
    .sel(rst), .in_0(demultiplexer_1_out_0), .in_1({5{1'b0}}), .out(multiplexer_10_out));
  Multiplexer #(.Bits(5)) multiplexer_11 (
    .sel(rst), .in_0(demultiplexer_1_out_1), .in_1({5{1'b0}}), .out(multiplexer_11_out));
  Multiplexer #(.Bits(5)) multiplexer_12 (
    .sel(rst), .in_0(demultiplexer_1_out_2), .in_1({5{1'b0}}), .out(multiplexer_12_out));
  Multiplexer #(.Bits(5)) multiplexer_13 (
    .sel(rst), .in_0(demultiplexer_1_out_3), .in_1({5{1'b0}}), .out(multiplexer_13_out));
  Multiplexer #(.Bits(5)) multiplexer_14 (
    .sel(rst), .in_0(demultiplexer_1_out_4), .in_1({5{1'b0}}), .out(multiplexer_14_out));
  Multiplexer #(.Bits(5)) multiplexer_15 (
    .sel(rst), .in_0(demultiplexer_1_out_5), .in_1({5{1'b0}}), .out(multiplexer_15_out));
  Multiplexer #(.Bits(5)) multiplexer_16 (
    .sel(rst), .in_0(demultiplexer_1_out_6), .in_1({5{1'b0}}), .out(multiplexer_16_out));
  Multiplexer #(.Bits(5)) multiplexer_17 (
    .sel(rst), .in_0(demultiplexer_1_out_7), .in_1({5{1'b0}}), .out(multiplexer_17_out));
  Demultiplexer #(.Selector_Bits(3)) demultiplexer_2 (
    .sel(counter_1_out), .in(1'b1), .out_0(demultiplexer_2_out_0), .out_1(demultiplexer_2_out_1),
    .out_2(demultiplexer_2_out_2), .out_3(demultiplexer_2_out_3), .out_4(demultiplexer_2_out_4),
    .out_5(demultiplexer_2_out_5), .out_6(demultiplexer_2_out_6), .out_7(demultiplexer_2_out_7));
  Multiplexer multiplexer_18 (.sel(rst), .in_0(1'b1), .in_1(1'b0), .out(multiplexer_18_out));
  or or_1 (or_1_out, demultiplexer_2_out_7, rst);
  and and_1 (and_1_out, demultiplexer_2_out_0, tc);
  and and_2 (and_2_out, demultiplexer_2_out_1, tc);
  and and_3 (and_3_out, demultiplexer_2_out_2, tc);
  and and_4 (and_4_out, demultiplexer_2_out_3, tc);
  and and_5 (and_5_out, demultiplexer_2_out_4, tc);
  and and_6 (and_6_out, demultiplexer_2_out_5, tc);
  and and_7 (and_7_out, demultiplexer_2_out_6, tc);
  and and_8 (and_8_out, demultiplexer_2_out_7, tc);
  Register register_1 (.D(multiplexer_18_out), .C(clk), .en(or_1_out), .Q(register_1_q));
  or or_2 (or_2_out, and_1_out, rst);
  or or_3 (or_3_out, and_2_out, rst);
  or or_4 (or_4_out, and_3_out, rst);
  or or_5 (or_5_out, and_4_out, rst);
  or or_6 (or_6_out, and_5_out, rst);
  or or_7 (or_7_out, and_6_out, rst);
  or or_8 (or_8_out, and_7_out, rst);
  or or_9 (or_9_out, and_8_out, rst);
  not not_1 (tc, register_1_q);
  Register #(.Bits(5)) r1 (.D(multiplexer_10_out), .C(clk), .en(or_2_out), .Q(o1));
  Register #(.Bits(5)) r2 (.D(multiplexer_11_out), .C(clk), .en(or_3_out), .Q(o2));
  Register #(.Bits(5)) r3 (.D(multiplexer_12_out), .C(clk), .en(or_4_out), .Q(o3));
  Register #(.Bits(5)) r4 (.D(multiplexer_13_out), .C(clk), .en(or_5_out), .Q(o4));
  Register #(.Bits(5)) r5 (.D(multiplexer_14_out), .C(clk), .en(or_6_out), .Q(o5));
  Register #(.Bits(5)) r6 (.D(multiplexer_15_out), .C(clk), .en(or_7_out), .Q(o6));
  Register #(.Bits(5)) r8 (.D(multiplexer_17_out), .C(clk), .en(or_9_out), .Q(o8));
  Register #(.Bits(5)) r7 (.D(multiplexer_16_out), .C(clk), .en(or_8_out), .Q(o7));

  // Notes on the sheet:
  //   rst: active_high
  //   w3
  //   w4
  //   w5
  //   w6
  //   w7
  //   w8
  //   w9
  //   a=>rom indexing
  //   a=>sequential rom Read
  //   contents of FilterKernel (hex, n*v repeats v):
  //   0,1,2,3,1,2,3,4,2,3,4,5,3,4,5,6,4,5,6,7,5,6,7,8,6,7,8,9,7,8,9
  //   ,a,2,3,4,5,3,4,5,6,4,5,6,7,5,6,7,8,6,7,8,9,7,8,9,a,8,9,a,b,9,a
  //   ,b,c,1,2,3,4,2,3,4,5,3,4,5,6,4,5,6,7,5,6,7,8,6,7,8,9,7,8,9,a,8
  //   ,9,a,b,3,4,5,6,4,5,6,7,5,6,7,8,6,7,8,9,7,8,9,a,8,9,a,b,9,a,b,c
  //   ,a,b,c,d,2,3,4,5,3,4,5,6,4,5,6,7,5,6,7,8,6,7,8,9,7,8,9,a,8,9,a
  //   ,b,9,a,b,c,4,5,6,7,5,6,7,8,6,7,8,9,7,8,9,a,8,9,a,b,9,a,b,c,a,b
  //   ,c,d,b,c,d,e,3,4,5,6,4,5,6,7,5,6,7,8,6,7,8,9,7,8,9,a,8,9,a,b,9
  //   ,a,b,c,a,b,c,d,5,6,7,8,6,7,8,9,7,8,9,a,8,9,a,b,9,a,b,c,a,b,c,d
  //   ,b,c,d,e,c,d,e,f,1,2,3,4,2,3,4,5,3,4,5,6,4,5,6,7,5,6,7,8,6,7,8
  //   ,9,7,8,9,a,8,9,a,b,3,4,5,6,4,5,6,7,5,6,7,8,6,7,8,9,7,8,9,a,8,9
  //   ,a,b,9,a,b,c,a,b,c,d,2,3,4,5,3,4,5,6,4,5,6,7,5,6,7,8,6,7,8,9,7
  //   ,8,9,a,8,9,a,b,9,a,b,c,4,5,6,7,5,6,7,8,6,7,8,9,7,8,9,a,8,9,a,b
  //   ,9,a,b,c,a,b,c,d,b,c,d,e,3,4,5,6,4,5,6,7,5,6,7,8,6,7,8,9,7,8,9
  //   ,a,8,9,a,b,9,a,b,c,a,b,c,d,5,6,7,8,6,7,8,9,7,8,9,a,8,9,a,b,9,a
  //   ,b,c,a,b,c,d,b,c,d,e,c,d,e,f,4,5,6,7,5,6,7,8,6,7,8,9,7,8,9,a,8
  //   ,9,a,b,9,a,b,c,a,b,c,d,b,c,d,e,6,7,8,9,7,8,9,a,8,9,a,b,9,a,b,c
  //   ,a,b,c,d,b,c,d,e,c,d,e,f,d,e,f,10
endmodule
