// Digital circuit SPIReader.dig as structural Verilog
module SPIReader (
  input  A0,
  input  A1,
  input  A2,
  input  A3,
  input  A4,
  input  A5,
  input  A6,
  input  A7,
  input  A8,
  input  A9,
  input  A10,
  input  A11,
  input  A12,
  input  A13,
  input  A14,
  input  A15,
  input  CLK,
  input  START,
  input  MISO,
  input  rst,
  output MOSI,
  output [7:0] R3,
  output [7:0] R2,
  output [7:0] R1,
  output [7:0] R0,
  output CS,
  output SCK,
  output DONE
);

  wire C3, C4, C5, C34, DPHASE, DRUN, LOADCYC, MHIN, MISOHOLD, multiplexer_1_out, multiplexer_2_out,
       multiplexer_3_out, multiplexer_4_out, multiplexer_5_out, multiplexer_6_out, multiplexer_7_out,
       multiplexer_8_out, multiplexer_9_out, multiplexer_10_out, multiplexer_12_out, multiplexer_13_out,
       multiplexer_14_out, multiplexer_15_out, multiplexer_16_out, multiplexer_17_out, multiplexer_18_out,
       multiplexer_19_out, multiplexer_20_out, multiplexer_21_out, multiplexer_22_out, multiplexer_23_out,
       multiplexer_24_out, multiplexer_25_out, multiplexer_26_out, multiplexer_27_out, multiplexer_28_out,
       multiplexer_29_out, multiplexer_30_out, multiplexer_31_out, multiplexer_32_out, multiplexer_33_out,
       multiplexer_34_out, multiplexer_35_out, multiplexer_36_out, multiplexer_37_out, multiplexer_38_out,
       multiplexer_39_out, multiplexer_40_out, multiplexer_41_out, multiplexer_42_out, multiplexer_43_out,
       multiplexer_44_out, multiplexer_45_out, multiplexer_46_out, multiplexer_47_out, multiplexer_48_out,
       multiplexer_49_out, multiplexer_50_out, multiplexer_51_out, multiplexer_52_out, multiplexer_53_out,
       multiplexer_54_out, multiplexer_55_out, multiplexer_56_out, multiplexer_57_out, multiplexer_58_out,
       multiplexer_59_out, multiplexer_60_out, multiplexer_61_out, multiplexer_62_out, multiplexer_63_out,
       multiplexer_64_out, multiplexer_65_out, multiplexer_66_out, multiplexer_67_out, multiplexer_68_out,
       multiplexer_69_out, multiplexer_70_out, multiplexer_71_out, multiplexer_72_out, multiplexer_73_out,
       multiplexer_74_out, multiplexer_75_out, multiplexer_76_out, multiplexer_77_out, multiplexer_78_out,
       multiplexer_79_out, multiplexer_80_out, multiplexer_81_out, multiplexer_82_out, multiplexer_83_out,
       multiplexer_84_out, multiplexer_85_out, multiplexer_86_out, multiplexer_87_out, multiplexer_88_out,
       multiplexer_89_out, multiplexer_90_out, multiplexer_91_out, multiplexer_92_out, multiplexer_93_out,
       multiplexer_94_out, multiplexer_95_out, multiplexer_96_out, multiplexer_97_out, multiplexer_98_out,
       multiplexer_99_out, multiplexer_100_out, multiplexer_101_out, multiplexer_102_out,
       multiplexer_103_out, multiplexer_104_out, multiplexer_105_out, multiplexer_106_out,
       multiplexer_107_out, multiplexer_108_out, multiplexer_109_out, multiplexer_110_out,
       multiplexer_111_out, multiplexer_112_out, multiplexer_113_out, multiplexer_114_out,
       multiplexer_115_out, multiplexer_116_out, multiplexer_117_out, NDONE, NPHASE, NSTARTPREV, PHASE, QH32,
       QH33, QH34, QH35, QH36, QH37, QH38, QH39, QH40, QH41, QH42, QH43, QH44, QH45, QH46, QH47, QH48, QH49,
       QH50, QH51, QH52, QH53, QH54, REGEN, RISEEN, RUN, SHIFT, SHIFTING, STARTEDGE, STARTPREV;
  wire [6:0] COUNT;

  and and_1 (C34, C3, C4);
  and and_2 (DONE, C34, C5);
  Multiplexer multiplexer_1 (.sel(rst), .in_0(DRUN), .in_1(1'b0), .out(multiplexer_1_out));
  Multiplexer multiplexer_2 (.sel(rst), .in_0(DPHASE), .in_1(1'b0), .out(multiplexer_2_out));
  Multiplexer multiplexer_3 (.sel(rst), .in_0(CS), .in_1(1'b1), .out(multiplexer_3_out));
  D_FF d_ff_1 (.D(multiplexer_1_out), .C(CLK), .Q(RUN));  // open: nQ
  D_FF d_ff_2 (.D(multiplexer_2_out), .C(CLK), .Q(PHASE));  // open: nQ
  Counter #(.Bits(7)) counter_1 (
    .en(SCK), .C(CLK), .clr(multiplexer_3_out), .out({COUNT[6], C5, C4, C3, COUNT[2:0]}));  // open: ovf
  Multiplexer multiplexer_4 (.sel(SHIFT), .in_0(1'b0), .in_1(MISOHOLD), .out(multiplexer_4_out));
  Multiplexer multiplexer_5 (.sel(REGEN), .in_0(R3[0]), .in_1(multiplexer_4_out), .out(multiplexer_5_out));
  not not_1 (CS, RUN);
  not not_2 (NPHASE, PHASE);
  D_FF d_ff_3 (.D(multiplexer_5_out), .C(CLK), .Q(R3[0]));  // open: nQ
  or or_1 (DRUN, LOADCYC, SHIFTING);
  and and_3 (DPHASE, RUN, NPHASE);
  Multiplexer multiplexer_6 (.sel(SHIFT), .in_0(1'b0), .in_1(R3[0]), .out(multiplexer_6_out));
  Multiplexer multiplexer_7 (.sel(REGEN), .in_0(R3[1]), .in_1(multiplexer_6_out), .out(multiplexer_7_out));
  D_FF d_ff_4 (.D(multiplexer_7_out), .C(CLK), .Q(R3[1]));  // open: nQ
  and and_4 (SHIFTING, RUN, NDONE);
  and and_5 (SCK, RUN, PHASE);
  and and_6 (RISEEN, RUN, NPHASE);
  not not_3 (NDONE, DONE);
  Multiplexer multiplexer_8 (.sel(SHIFT), .in_0(1'b0), .in_1(R3[1]), .out(multiplexer_8_out));
  Multiplexer multiplexer_9 (.sel(REGEN), .in_0(R3[2]), .in_1(multiplexer_8_out), .out(multiplexer_9_out));
  D_FF d_ff_5 (.D(multiplexer_9_out), .C(CLK), .Q(R3[2]));  // open: nQ
  not not_4 (SHIFT, LOADCYC);
  Multiplexer multiplexer_10 (.sel(SHIFT), .in_0(1'b0), .in_1(R3[2]), .out(multiplexer_10_out));
  and and_7 (LOADCYC, STARTEDGE, CS);
  or or_2 (REGEN, LOADCYC, SCK);
  Multiplexer multiplexer_11 (.sel(RISEEN), .in_0(MISOHOLD), .in_1(MISO), .out(MHIN));
  Multiplexer multiplexer_12 (.sel(REGEN), .in_0(R3[3]), .in_1(multiplexer_10_out), .out(multiplexer_12_out));
  D_FF d_ff_6 (.D(multiplexer_12_out), .C(CLK), .Q(R3[3]));  // open: nQ
  Multiplexer multiplexer_13 (.sel(rst), .in_0(START), .in_1(1'b1), .out(multiplexer_13_out));
  D_FF d_ff_7 (.D(multiplexer_13_out), .C(CLK), .Q(STARTPREV));  // open: nQ
  Multiplexer multiplexer_14 (.sel(SHIFT), .in_0(1'b0), .in_1(R3[3]), .out(multiplexer_14_out));
  D_FF d_ff_8 (.D(MHIN), .C(CLK), .Q(MISOHOLD));  // open: nQ
  Multiplexer multiplexer_15 (.sel(REGEN), .in_0(R3[4]), .in_1(multiplexer_14_out), .out(multiplexer_15_out));
  D_FF d_ff_9 (.D(multiplexer_15_out), .C(CLK), .Q(R3[4]));  // open: nQ
  not not_5 (NSTARTPREV, STARTPREV);
  Multiplexer multiplexer_16 (.sel(SHIFT), .in_0(1'b0), .in_1(R3[4]), .out(multiplexer_16_out));
  and and_8 (STARTEDGE, START, NSTARTPREV);
  Multiplexer multiplexer_17 (.sel(REGEN), .in_0(R3[5]), .in_1(multiplexer_16_out), .out(multiplexer_17_out));
  D_FF d_ff_10 (.D(multiplexer_17_out), .C(CLK), .Q(R3[5]));  // open: nQ
  Multiplexer multiplexer_18 (.sel(SHIFT), .in_0(1'b0), .in_1(R3[5]), .out(multiplexer_18_out));
  Multiplexer multiplexer_19 (.sel(REGEN), .in_0(R3[6]), .in_1(multiplexer_18_out), .out(multiplexer_19_out));
  D_FF d_ff_11 (.D(multiplexer_19_out), .C(CLK), .Q(R3[6]));  // open: nQ
  Multiplexer multiplexer_20 (.sel(SHIFT), .in_0(1'b0), .in_1(R3[6]), .out(multiplexer_20_out));
  Multiplexer multiplexer_21 (.sel(REGEN), .in_0(R3[7]), .in_1(multiplexer_20_out), .out(multiplexer_21_out));
  D_FF d_ff_12 (.D(multiplexer_21_out), .C(CLK), .Q(R3[7]));  // open: nQ
  Multiplexer multiplexer_22 (.sel(SHIFT), .in_0(1'b0), .in_1(R3[7]), .out(multiplexer_22_out));
  Multiplexer multiplexer_23 (.sel(REGEN), .in_0(R2[0]), .in_1(multiplexer_22_out), .out(multiplexer_23_out));
  D_FF d_ff_13 (.D(multiplexer_23_out), .C(CLK), .Q(R2[0]));  // open: nQ
  Multiplexer multiplexer_24 (.sel(SHIFT), .in_0(1'b0), .in_1(R2[0]), .out(multiplexer_24_out));
  Multiplexer multiplexer_25 (.sel(REGEN), .in_0(R2[1]), .in_1(multiplexer_24_out), .out(multiplexer_25_out));
  D_FF d_ff_14 (.D(multiplexer_25_out), .C(CLK), .Q(R2[1]));  // open: nQ
  Multiplexer multiplexer_26 (.sel(SHIFT), .in_0(1'b0), .in_1(R2[1]), .out(multiplexer_26_out));
  Multiplexer multiplexer_27 (.sel(REGEN), .in_0(R2[2]), .in_1(multiplexer_26_out), .out(multiplexer_27_out));
  D_FF d_ff_15 (.D(multiplexer_27_out), .C(CLK), .Q(R2[2]));  // open: nQ
  Multiplexer multiplexer_28 (.sel(SHIFT), .in_0(1'b0), .in_1(R2[2]), .out(multiplexer_28_out));
  Multiplexer multiplexer_29 (.sel(REGEN), .in_0(R2[3]), .in_1(multiplexer_28_out), .out(multiplexer_29_out));
  D_FF d_ff_16 (.D(multiplexer_29_out), .C(CLK), .Q(R2[3]));  // open: nQ
  Multiplexer multiplexer_30 (.sel(SHIFT), .in_0(1'b0), .in_1(R2[3]), .out(multiplexer_30_out));
  Multiplexer multiplexer_31 (.sel(REGEN), .in_0(R2[4]), .in_1(multiplexer_30_out), .out(multiplexer_31_out));
  D_FF d_ff_17 (.D(multiplexer_31_out), .C(CLK), .Q(R2[4]));  // open: nQ
  Multiplexer multiplexer_32 (.sel(SHIFT), .in_0(1'b0), .in_1(R2[4]), .out(multiplexer_32_out));
  Multiplexer multiplexer_33 (.sel(REGEN), .in_0(R2[5]), .in_1(multiplexer_32_out), .out(multiplexer_33_out));
  D_FF d_ff_18 (.D(multiplexer_33_out), .C(CLK), .Q(R2[5]));  // open: nQ
  Multiplexer multiplexer_34 (.sel(SHIFT), .in_0(1'b0), .in_1(R2[5]), .out(multiplexer_34_out));
  Multiplexer multiplexer_35 (.sel(REGEN), .in_0(R2[6]), .in_1(multiplexer_34_out), .out(multiplexer_35_out));
  D_FF d_ff_19 (.D(multiplexer_35_out), .C(CLK), .Q(R2[6]));  // open: nQ
  Multiplexer multiplexer_36 (.sel(SHIFT), .in_0(1'b0), .in_1(R2[6]), .out(multiplexer_36_out));
  Multiplexer multiplexer_37 (.sel(REGEN), .in_0(R2[7]), .in_1(multiplexer_36_out), .out(multiplexer_37_out));
  D_FF d_ff_20 (.D(multiplexer_37_out), .C(CLK), .Q(R2[7]));  // open: nQ
  Multiplexer multiplexer_38 (.sel(SHIFT), .in_0(1'b0), .in_1(R2[7]), .out(multiplexer_38_out));
  Multiplexer multiplexer_39 (.sel(REGEN), .in_0(R1[0]), .in_1(multiplexer_38_out), .out(multiplexer_39_out));
  D_FF d_ff_21 (.D(multiplexer_39_out), .C(CLK), .Q(R1[0]));  // open: nQ
  Multiplexer multiplexer_40 (.sel(SHIFT), .in_0(1'b0), .in_1(R1[0]), .out(multiplexer_40_out));
  Multiplexer multiplexer_41 (.sel(REGEN), .in_0(R1[1]), .in_1(multiplexer_40_out), .out(multiplexer_41_out));
  D_FF d_ff_22 (.D(multiplexer_41_out), .C(CLK), .Q(R1[1]));  // open: nQ
  Multiplexer multiplexer_42 (.sel(SHIFT), .in_0(1'b0), .in_1(R1[1]), .out(multiplexer_42_out));
  Multiplexer multiplexer_43 (.sel(REGEN), .in_0(R1[2]), .in_1(multiplexer_42_out), .out(multiplexer_43_out));
  D_FF d_ff_23 (.D(multiplexer_43_out), .C(CLK), .Q(R1[2]));  // open: nQ
  Multiplexer multiplexer_44 (.sel(SHIFT), .in_0(1'b0), .in_1(R1[2]), .out(multiplexer_44_out));
  Multiplexer multiplexer_45 (.sel(REGEN), .in_0(R1[3]), .in_1(multiplexer_44_out), .out(multiplexer_45_out));
  D_FF d_ff_24 (.D(multiplexer_45_out), .C(CLK), .Q(R1[3]));  // open: nQ
  Multiplexer multiplexer_46 (.sel(SHIFT), .in_0(1'b0), .in_1(R1[3]), .out(multiplexer_46_out));
  Multiplexer multiplexer_47 (.sel(REGEN), .in_0(R1[4]), .in_1(multiplexer_46_out), .out(multiplexer_47_out));
  D_FF d_ff_25 (.D(multiplexer_47_out), .C(CLK), .Q(R1[4]));  // open: nQ
  Multiplexer multiplexer_48 (.sel(SHIFT), .in_0(1'b0), .in_1(R1[4]), .out(multiplexer_48_out));
  Multiplexer multiplexer_49 (.sel(REGEN), .in_0(R1[5]), .in_1(multiplexer_48_out), .out(multiplexer_49_out));
  D_FF d_ff_26 (.D(multiplexer_49_out), .C(CLK), .Q(R1[5]));  // open: nQ
  Multiplexer multiplexer_50 (.sel(SHIFT), .in_0(1'b0), .in_1(R1[5]), .out(multiplexer_50_out));
  Multiplexer multiplexer_51 (.sel(REGEN), .in_0(R1[6]), .in_1(multiplexer_50_out), .out(multiplexer_51_out));
  D_FF d_ff_27 (.D(multiplexer_51_out), .C(CLK), .Q(R1[6]));  // open: nQ
  Multiplexer multiplexer_52 (.sel(SHIFT), .in_0(1'b0), .in_1(R1[6]), .out(multiplexer_52_out));
  Multiplexer multiplexer_53 (.sel(REGEN), .in_0(R1[7]), .in_1(multiplexer_52_out), .out(multiplexer_53_out));
  D_FF d_ff_28 (.D(multiplexer_53_out), .C(CLK), .Q(R1[7]));  // open: nQ
  Multiplexer multiplexer_54 (.sel(SHIFT), .in_0(1'b0), .in_1(R1[7]), .out(multiplexer_54_out));
  Multiplexer multiplexer_55 (.sel(REGEN), .in_0(R0[0]), .in_1(multiplexer_54_out), .out(multiplexer_55_out));
  D_FF d_ff_29 (.D(multiplexer_55_out), .C(CLK), .Q(R0[0]));  // open: nQ
  Multiplexer multiplexer_56 (.sel(SHIFT), .in_0(1'b0), .in_1(R0[0]), .out(multiplexer_56_out));
  Multiplexer multiplexer_57 (.sel(REGEN), .in_0(R0[1]), .in_1(multiplexer_56_out), .out(multiplexer_57_out));
  D_FF d_ff_30 (.D(multiplexer_57_out), .C(CLK), .Q(R0[1]));  // open: nQ
  Multiplexer multiplexer_58 (.sel(SHIFT), .in_0(1'b0), .in_1(R0[1]), .out(multiplexer_58_out));
  Multiplexer multiplexer_59 (.sel(REGEN), .in_0(R0[2]), .in_1(multiplexer_58_out), .out(multiplexer_59_out));
  D_FF d_ff_31 (.D(multiplexer_59_out), .C(CLK), .Q(R0[2]));  // open: nQ
  Multiplexer multiplexer_60 (.sel(SHIFT), .in_0(1'b0), .in_1(R0[2]), .out(multiplexer_60_out));
  Multiplexer multiplexer_61 (.sel(REGEN), .in_0(R0[3]), .in_1(multiplexer_60_out), .out(multiplexer_61_out));
  D_FF d_ff_32 (.D(multiplexer_61_out), .C(CLK), .Q(R0[3]));  // open: nQ
  Multiplexer multiplexer_62 (.sel(SHIFT), .in_0(1'b0), .in_1(R0[3]), .out(multiplexer_62_out));
  Multiplexer multiplexer_63 (.sel(REGEN), .in_0(R0[4]), .in_1(multiplexer_62_out), .out(multiplexer_63_out));
  D_FF d_ff_33 (.D(multiplexer_63_out), .C(CLK), .Q(R0[4]));  // open: nQ
  Multiplexer multiplexer_64 (.sel(SHIFT), .in_0(1'b0), .in_1(R0[4]), .out(multiplexer_64_out));
  Multiplexer multiplexer_65 (.sel(REGEN), .in_0(R0[5]), .in_1(multiplexer_64_out), .out(multiplexer_65_out));
  D_FF d_ff_34 (.D(multiplexer_65_out), .C(CLK), .Q(R0[5]));  // open: nQ
  Multiplexer multiplexer_66 (.sel(SHIFT), .in_0(1'b0), .in_1(R0[5]), .out(multiplexer_66_out));
  Multiplexer multiplexer_67 (.sel(REGEN), .in_0(R0[6]), .in_1(multiplexer_66_out), .out(multiplexer_67_out));
  D_FF d_ff_35 (.D(multiplexer_67_out), .C(CLK), .Q(R0[6]));  // open: nQ
  Multiplexer multiplexer_68 (.sel(SHIFT), .in_0(1'b0), .in_1(R0[6]), .out(multiplexer_68_out));
  Multiplexer multiplexer_69 (.sel(REGEN), .in_0(R0[7]), .in_1(multiplexer_68_out), .out(multiplexer_69_out));
  D_FF d_ff_36 (.D(multiplexer_69_out), .C(CLK), .Q(R0[7]));  // open: nQ
  Multiplexer multiplexer_70 (.sel(SHIFT), .in_0(A0), .in_1(R0[7]), .out(multiplexer_70_out));
  Multiplexer multiplexer_71 (.sel(REGEN), .in_0(QH32), .in_1(multiplexer_70_out), .out(multiplexer_71_out));
  D_FF d_ff_37 (.D(multiplexer_71_out), .C(CLK), .Q(QH32));  // open: nQ
  Multiplexer multiplexer_72 (.sel(SHIFT), .in_0(A1), .in_1(QH32), .out(multiplexer_72_out));
  Multiplexer multiplexer_73 (.sel(REGEN), .in_0(QH33), .in_1(multiplexer_72_out), .out(multiplexer_73_out));
  D_FF d_ff_38 (.D(multiplexer_73_out), .C(CLK), .Q(QH33));  // open: nQ
  Multiplexer multiplexer_74 (.sel(SHIFT), .in_0(A2), .in_1(QH33), .out(multiplexer_74_out));
  Multiplexer multiplexer_75 (.sel(REGEN), .in_0(QH34), .in_1(multiplexer_74_out), .out(multiplexer_75_out));
  D_FF d_ff_39 (.D(multiplexer_75_out), .C(CLK), .Q(QH34));  // open: nQ
  Multiplexer multiplexer_76 (.sel(SHIFT), .in_0(A3), .in_1(QH34), .out(multiplexer_76_out));
  Multiplexer multiplexer_77 (.sel(REGEN), .in_0(QH35), .in_1(multiplexer_76_out), .out(multiplexer_77_out));
  D_FF d_ff_40 (.D(multiplexer_77_out), .C(CLK), .Q(QH35));  // open: nQ
  Multiplexer multiplexer_78 (.sel(SHIFT), .in_0(A4), .in_1(QH35), .out(multiplexer_78_out));
  Multiplexer multiplexer_79 (.sel(REGEN), .in_0(QH36), .in_1(multiplexer_78_out), .out(multiplexer_79_out));
  D_FF d_ff_41 (.D(multiplexer_79_out), .C(CLK), .Q(QH36));  // open: nQ
  Multiplexer multiplexer_80 (.sel(SHIFT), .in_0(A5), .in_1(QH36), .out(multiplexer_80_out));
  Multiplexer multiplexer_81 (.sel(REGEN), .in_0(QH37), .in_1(multiplexer_80_out), .out(multiplexer_81_out));
  D_FF d_ff_42 (.D(multiplexer_81_out), .C(CLK), .Q(QH37));  // open: nQ
  Multiplexer multiplexer_82 (.sel(SHIFT), .in_0(A6), .in_1(QH37), .out(multiplexer_82_out));
  Multiplexer multiplexer_83 (.sel(REGEN), .in_0(QH38), .in_1(multiplexer_82_out), .out(multiplexer_83_out));
  D_FF d_ff_43 (.D(multiplexer_83_out), .C(CLK), .Q(QH38));  // open: nQ
  Multiplexer multiplexer_84 (.sel(SHIFT), .in_0(A7), .in_1(QH38), .out(multiplexer_84_out));
  Multiplexer multiplexer_85 (.sel(REGEN), .in_0(QH39), .in_1(multiplexer_84_out), .out(multiplexer_85_out));
  D_FF d_ff_44 (.D(multiplexer_85_out), .C(CLK), .Q(QH39));  // open: nQ
  Multiplexer multiplexer_86 (.sel(SHIFT), .in_0(A8), .in_1(QH39), .out(multiplexer_86_out));
  Multiplexer multiplexer_87 (.sel(REGEN), .in_0(QH40), .in_1(multiplexer_86_out), .out(multiplexer_87_out));
  D_FF d_ff_45 (.D(multiplexer_87_out), .C(CLK), .Q(QH40));  // open: nQ
  Multiplexer multiplexer_88 (.sel(SHIFT), .in_0(A9), .in_1(QH40), .out(multiplexer_88_out));
  Multiplexer multiplexer_89 (.sel(REGEN), .in_0(QH41), .in_1(multiplexer_88_out), .out(multiplexer_89_out));
  D_FF d_ff_46 (.D(multiplexer_89_out), .C(CLK), .Q(QH41));  // open: nQ
  Multiplexer multiplexer_90 (.sel(SHIFT), .in_0(A10), .in_1(QH41), .out(multiplexer_90_out));
  Multiplexer multiplexer_91 (.sel(REGEN), .in_0(QH42), .in_1(multiplexer_90_out), .out(multiplexer_91_out));
  D_FF d_ff_47 (.D(multiplexer_91_out), .C(CLK), .Q(QH42));  // open: nQ
  Multiplexer multiplexer_92 (.sel(SHIFT), .in_0(A11), .in_1(QH42), .out(multiplexer_92_out));
  Multiplexer multiplexer_93 (.sel(REGEN), .in_0(QH43), .in_1(multiplexer_92_out), .out(multiplexer_93_out));
  D_FF d_ff_48 (.D(multiplexer_93_out), .C(CLK), .Q(QH43));  // open: nQ
  Multiplexer multiplexer_94 (.sel(SHIFT), .in_0(A12), .in_1(QH43), .out(multiplexer_94_out));
  Multiplexer multiplexer_95 (.sel(REGEN), .in_0(QH44), .in_1(multiplexer_94_out), .out(multiplexer_95_out));
  D_FF d_ff_49 (.D(multiplexer_95_out), .C(CLK), .Q(QH44));  // open: nQ
  Multiplexer multiplexer_96 (.sel(SHIFT), .in_0(A13), .in_1(QH44), .out(multiplexer_96_out));
  Multiplexer multiplexer_97 (.sel(REGEN), .in_0(QH45), .in_1(multiplexer_96_out), .out(multiplexer_97_out));
  D_FF d_ff_50 (.D(multiplexer_97_out), .C(CLK), .Q(QH45));  // open: nQ
  Multiplexer multiplexer_98 (.sel(SHIFT), .in_0(A14), .in_1(QH45), .out(multiplexer_98_out));
  Multiplexer multiplexer_99 (.sel(REGEN), .in_0(QH46), .in_1(multiplexer_98_out), .out(multiplexer_99_out));
  D_FF d_ff_51 (.D(multiplexer_99_out), .C(CLK), .Q(QH46));  // open: nQ
  Multiplexer multiplexer_100 (.sel(SHIFT), .in_0(A15), .in_1(QH46), .out(multiplexer_100_out));
  Multiplexer multiplexer_101 (.sel(REGEN), .in_0(QH47), .in_1(multiplexer_100_out), .out(multiplexer_101_out));
  D_FF d_ff_52 (.D(multiplexer_101_out), .C(CLK), .Q(QH47));  // open: nQ
  Multiplexer multiplexer_102 (.sel(SHIFT), .in_0(1'b1), .in_1(QH47), .out(multiplexer_102_out));
  Multiplexer multiplexer_103 (.sel(REGEN), .in_0(QH48), .in_1(multiplexer_102_out), .out(multiplexer_103_out));
  D_FF d_ff_53 (.D(multiplexer_103_out), .C(CLK), .Q(QH48));  // open: nQ
  Multiplexer multiplexer_104 (.sel(SHIFT), .in_0(1'b1), .in_1(QH48), .out(multiplexer_104_out));
  Multiplexer multiplexer_105 (.sel(REGEN), .in_0(QH49), .in_1(multiplexer_104_out), .out(multiplexer_105_out));
  D_FF d_ff_54 (.D(multiplexer_105_out), .C(CLK), .Q(QH49));  // open: nQ
  Multiplexer multiplexer_106 (.sel(SHIFT), .in_0(1'b0), .in_1(QH49), .out(multiplexer_106_out));
  Multiplexer multiplexer_107 (.sel(REGEN), .in_0(QH50), .in_1(multiplexer_106_out), .out(multiplexer_107_out));
  D_FF d_ff_55 (.D(multiplexer_107_out), .C(CLK), .Q(QH50));  // open: nQ
  Multiplexer multiplexer_108 (.sel(SHIFT), .in_0(1'b0), .in_1(QH50), .out(multiplexer_108_out));
  Multiplexer multiplexer_109 (.sel(REGEN), .in_0(QH51), .in_1(multiplexer_108_out), .out(multiplexer_109_out));
  D_FF d_ff_56 (.D(multiplexer_109_out), .C(CLK), .Q(QH51));  // open: nQ
  Multiplexer multiplexer_110 (.sel(SHIFT), .in_0(1'b0), .in_1(QH51), .out(multiplexer_110_out));
  Multiplexer multiplexer_111 (.sel(REGEN), .in_0(QH52), .in_1(multiplexer_110_out), .out(multiplexer_111_out));
  D_FF d_ff_57 (.D(multiplexer_111_out), .C(CLK), .Q(QH52));  // open: nQ
  Multiplexer multiplexer_112 (.sel(SHIFT), .in_0(1'b0), .in_1(QH52), .out(multiplexer_112_out));
  Multiplexer multiplexer_113 (.sel(REGEN), .in_0(QH53), .in_1(multiplexer_112_out), .out(multiplexer_113_out));
  D_FF d_ff_58 (.D(multiplexer_113_out), .C(CLK), .Q(QH53));  // open: nQ
  Multiplexer multiplexer_114 (.sel(SHIFT), .in_0(1'b0), .in_1(QH53), .out(multiplexer_114_out));
  Multiplexer multiplexer_115 (.sel(REGEN), .in_0(QH54), .in_1(multiplexer_114_out), .out(multiplexer_115_out));
  D_FF d_ff_59 (.D(multiplexer_115_out), .C(CLK), .Q(QH54));  // open: nQ
  Multiplexer multiplexer_116 (.sel(SHIFT), .in_0(1'b0), .in_1(QH54), .out(multiplexer_116_out));
  Multiplexer multiplexer_117 (.sel(REGEN), .in_0(MOSI), .in_1(multiplexer_116_out), .out(multiplexer_117_out));
  D_FF d_ff_60 (.D(multiplexer_117_out), .C(CLK), .Q(MOSI));  // open: nQ

  // Other names for the same wires on the sheet: COUNT[5:3] = {C5, C4, C3}; NRUN = CS; PEND = SCK; QH0 = R3[0];
  //   QH1 = R3[1]; QH2 = R3[2]; QH3 = R3[3]; QH4 = R3[4]; QH5 = R3[5]; QH6 = R3[6]; QH7 = R3[7]; QH8 = R2[0];
  //   QH9 = R2[1]; QH10 = R2[2]; QH11 = R2[3]; QH12 = R2[4]; QH13 = R2[5]; QH14 = R2[6]; QH15 = R2[7]; QH16 = R1[0];
  //   QH17 = R1[1]; QH18 = R1[2]; QH19 = R1[3]; QH20 = R1[4]; QH21 = R1[5]; QH22 = R1[6]; QH23 = R1[7]; QH24 = R0[0];
  //   QH25 = R0[1]; QH26 = R0[2]; QH27 = R0[3]; QH28 = R0[4]; QH29 = R0[5]; QH30 = R0[6]; QH31 = R0[7]; QH55 = MOSI
endmodule
