// Digital circuit TinyTapeoutAdderTreeOhneHdc.dig as structural Verilog
module TinyTapeoutAdderTreeOhneHdc (
  input  [7:0] ui_in,
  input  clk,
  input  [7:0] uio_in,
  input  rst,
  output [7:0] uo_out
);

  wire and_1_out, and_2_out, and_3_out, and_4_out, and_5_out, and_6_out, and_7_out, and_8_out, and_9_out,
       demultiplexer_1_out_0, demultiplexer_1_out_1, demultiplexer_1_out_2, demultiplexer_1_out_3,
       demultiplexer_1_out_4, demultiplexer_1_out_5, demultiplexer_1_out_6, demultiplexer_1_out_7,
       demultiplexer_1_out_8, or_1_out, or_2_out, or_3_out, or_4_out, or_5_out, or_6_out, or_7_out, or_8_out,
       or_9_out;
  wire [1:0] _8bit_bsd_tc_adder_3_c, _8bit_bsd_tc_adder_6_c;
  wire [3:0] _13bitbsd_1_out_4;
  wire [4:0] rominterpretation_1_o1, rominterpretation_1_o2, rominterpretation_1_o3, rominterpretation_1_o4,
       rominterpretation_1_o5, rominterpretation_1_o6, rominterpretation_1_o7, rominterpretation_1_o8;
  wire [7:0] _5auf8_1_ou5, _5auf8_2_ou5, _5auf8_3_ou5, _5auf8_4_ou5, _5auf8_5_ou5, _5auf8_6_ou5,
       _13bitbsd_1_out, _13bitbsd_1_out_2, _13bitbsd_1_out_3, multiplexer_1_out, shift1_1_out, shift1_2_out,
       shift2_1_out, shift2_2_out, shift3_1_out, shift3_2_out, t1, t2, t3, t4, t5, t6, t7, t8, t9;
  wire [15:0] _8bit_bsd_tc_adder_1_bsdout, _8bit_bsd_tc_adder_2_bsdout, _8bit_bsd_tc_adder_3_bsdout,
       _8bit_bsd_tc_adder_4_bsdout, _8bit_bsd_tc_adder_5_bsdout, _8bit_bsd_tc_adder_6_bsdout,
       conv5to8_1__10bdd, conv5to8_2__10bdd;
  wire [25:0] _18auf24_1_ou5, shift4_1_out;

  Demultiplexer #(.Selector_Bits(4)) demultiplexer_1 (
    .sel(uio_in[3:0]), .in(1'b1), .out_0(demultiplexer_1_out_0), .out_1(demultiplexer_1_out_1),
    .out_2(demultiplexer_1_out_2), .out_3(demultiplexer_1_out_3), .out_4(demultiplexer_1_out_4),
    .out_5(demultiplexer_1_out_5), .out_6(demultiplexer_1_out_6), .out_7(demultiplexer_1_out_7),
    .out_8(demultiplexer_1_out_8));  // open: out_9, out_10, out_11, out_12, out_13, out_14, out_15
  Multiplexer #(.Bits(8)) multiplexer_1 (.sel(rst), .in_0(ui_in), .in_1({8{1'b0}}), .out(multiplexer_1_out));
  and and_1 (and_1_out, demultiplexer_1_out_0, uio_in[7]);
  and and_2 (and_2_out, demultiplexer_1_out_1, uio_in[7]);
  and and_3 (and_3_out, demultiplexer_1_out_2, uio_in[7]);
  and and_4 (and_4_out, demultiplexer_1_out_3, uio_in[7]);
  and and_5 (and_5_out, demultiplexer_1_out_4, uio_in[7]);
  and and_6 (and_6_out, demultiplexer_1_out_5, uio_in[7]);
  and and_7 (and_7_out, demultiplexer_1_out_6, uio_in[7]);
  and and_8 (and_8_out, demultiplexer_1_out_7, uio_in[7]);
  and and_9 (and_9_out, demultiplexer_1_out_8, uio_in[7]);
  or or_1 (or_1_out, and_1_out, rst);
  or or_2 (or_2_out, and_2_out, rst);
  or or_3 (or_3_out, and_3_out, rst);
  or or_4 (or_4_out, and_4_out, rst);
  or or_5 (or_5_out, and_5_out, rst);
  or or_6 (or_6_out, and_6_out, rst);
  or or_7 (or_7_out, and_7_out, rst);
  or or_8 (or_8_out, and_8_out, rst);
  or or_9 (or_9_out, and_9_out, rst);
  Register #(.Bits(8)) R0 (.D(multiplexer_1_out), .C(clk), .en(or_1_out), .Q(t1));
  Register #(.Bits(8)) R1 (.D(multiplexer_1_out), .C(clk), .en(or_2_out), .Q(t2));
  Register #(.Bits(8)) R2 (.D(multiplexer_1_out), .C(clk), .en(or_3_out), .Q(t3));
  Register #(.Bits(8)) R3 (.D(multiplexer_1_out), .C(clk), .en(or_4_out), .Q(t4));
  Register #(.Bits(8)) R4 (.D(multiplexer_1_out), .C(clk), .en(or_5_out), .Q(t5));
  Register #(.Bits(8)) R5 (.D(multiplexer_1_out), .C(clk), .en(or_6_out), .Q(t6));
  Register #(.Bits(8)) R6 (.D(multiplexer_1_out), .C(clk), .en(or_7_out), .Q(t7));
  Register #(.Bits(8)) R7 (.D(multiplexer_1_out), .C(clk), .en(or_8_out), .Q(t8));
  Register #(.Bits(8)) R8 (.D(multiplexer_1_out), .C(clk), .en(or_9_out), .Q(t9));
  conv5to8 conv5to8_1 (.in(rominterpretation_1_o1), ._10bdd(conv5to8_1__10bdd));
  _8bit_BSD_TC_Adder _8bit_bsd_tc_adder_1 (
    .inTC(shift1_1_out), .inBSD(conv5to8_1__10bdd), .bsdOut(_8bit_bsd_tc_adder_1_bsdout));  // open: c
  _5auf8 _5auf8_1 (.in(rominterpretation_1_o2), .ou5(_5auf8_1_ou5));
  shift1 shift1_1 (.in(_5auf8_1_ou5), .out(shift1_1_out));
  _8bit_BSD_TC_Adder _8bit_bsd_tc_adder_2 (
    .inTC(shift2_1_out), .inBSD(_8bit_bsd_tc_adder_1_bsdout), .bsdOut(_8bit_bsd_tc_adder_2_bsdout));  // open: c
  RomInterpretation rominterpretation_1 (
    .w3(t3), .w4(t4), .w5(t5), .w6(t6), .w7(t7), .w8(t8), .w9(t9), .w1(t1), .w2(t2), .clk(clk),
    .en(uio_in[6]), .rst(rst), .o1(rominterpretation_1_o1), .o2(rominterpretation_1_o2),
    .o3(rominterpretation_1_o3), .o4(rominterpretation_1_o4), .o5(rominterpretation_1_o5),
    .o6(rominterpretation_1_o6), .o7(rominterpretation_1_o7), .o8(rominterpretation_1_o8));
  _5auf8 _5auf8_2 (.in(rominterpretation_1_o3), .ou5(_5auf8_2_ou5));
  shift2 shift2_1 (.in(_5auf8_2_ou5), .out(shift2_1_out));
  _8bit_BSD_TC_Adder _8bit_bsd_tc_adder_3 (
    .inTC(shift3_1_out), .inBSD(_8bit_bsd_tc_adder_2_bsdout), .bsdOut(_8bit_bsd_tc_adder_3_bsdout),
    .c(_8bit_bsd_tc_adder_3_c));
  _18auf24 _18auf24_1 (.in({_8bit_bsd_tc_adder_3_c, _8bit_bsd_tc_adder_3_bsdout}), .ou5(_18auf24_1_ou5));
  _5auf8 _5auf8_3 (.in(rominterpretation_1_o4), .ou5(_5auf8_3_ou5));
  shift3 shift3_1 (.in(_5auf8_3_ou5), .out(shift3_1_out));
  conv5to8 conv5to8_2 (.in(rominterpretation_1_o5), ._10bdd(conv5to8_2__10bdd));
  _8bit_BSD_TC_Adder _8bit_bsd_tc_adder_4 (
    .inTC(shift1_2_out), .inBSD(conv5to8_2__10bdd), .bsdOut(_8bit_bsd_tc_adder_4_bsdout));  // open: c
  _5auf8 _5auf8_4 (.in(rominterpretation_1_o6), .ou5(_5auf8_4_ou5));
  shift1 shift1_2 (.in(_5auf8_4_ou5), .out(shift1_2_out));
  _13BitBSD _13bitbsd_1 (
    .inA(shift4_1_out), .inB(_18auf24_1_ou5),
    .out({_13bitbsd_1_out_4, _13bitbsd_1_out_3, _13bitbsd_1_out_2, _13bitbsd_1_out}));
  Multiplexer #(.Selector_Bits(2), .Bits(8)) multiplexer_2 (
    .sel(uio_in[5:4]), .in_0(_13bitbsd_1_out), .in_1(_13bitbsd_1_out_2), .in_2(_13bitbsd_1_out_3),
    .in_3({4'b0101, _13bitbsd_1_out_4}), .out(uo_out));
  _8bit_BSD_TC_Adder _8bit_bsd_tc_adder_5 (
    .inTC(shift2_2_out), .inBSD(_8bit_bsd_tc_adder_4_bsdout), .bsdOut(_8bit_bsd_tc_adder_5_bsdout));  // open: c
  _5auf8 _5auf8_5 (.in(rominterpretation_1_o7), .ou5(_5auf8_5_ou5));
  shift2 shift2_2 (.in(_5auf8_5_ou5), .out(shift2_2_out));
  shift4 shift4_1 (.in({_8bit_bsd_tc_adder_6_c, _8bit_bsd_tc_adder_6_bsdout}), .out(shift4_1_out));
  _8bit_BSD_TC_Adder _8bit_bsd_tc_adder_6 (
    .inTC(shift3_2_out), .inBSD(_8bit_bsd_tc_adder_5_bsdout), .bsdOut(_8bit_bsd_tc_adder_6_bsdout),
    .c(_8bit_bsd_tc_adder_6_c));
  _5auf8 _5auf8_6 (.in(rominterpretation_1_o8), .ou5(_5auf8_6_ou5));
  shift3 shift3_2 (.in(_5auf8_6_ou5), .out(shift3_2_out));

  // Other names for the same wires on the sheet: en = uio_in[6]; write = uio_in[7]

  // Notes on the sheet:
  //   uio_in: 0,1,2,3 => reg mux
  //   4,5 => sel out
  //   6,7 => en, write
  //   5bit
  //   8 bit bsd adder
  //   8 out (safe)
  //   im Rom liegen pos binary werte
  //   9 bit BSD out
  //   13 bit BSD
  //   13 bit BSD adder
  //   16bit
  //   9 bit BSD Adder
endmodule
